// Logisim project кобяшова д.а.circ as structural Verilog: 5 circuits, main circuit мультиплексор
module \мультиплексор  (
  input  _0,
  input  _1,
  input  in_3,
  input  in_4,
  input  in_5,
  input  in_6,
  input  in_7,
  input  in_8,
  input  in_9,
  input  in_10,
  input  in_11,
  input  in_12,
  input  in_13,
  input  in_14,
  input  in_15,
  input  in_16,
  input  in_17,
  input  in_18,
  input  in_19,
  input  in_20,
  output \выход 
);

  wire and_1_out, and_2_out, and_3_out, and_4_out, and_5_out, and_6_out, and_7_out, and_8_out, and_9_out,
       and_10_out, and_11_out, and_12_out, and_13_out, and_14_out, and_15_out, and_16_out, not_1_out,
       not_3_out, not_4_out;

  not not_1 (not_1_out, in_17);
  not not_2 (not_1_out, in_18);
  not not_3 (not_3_out, in_19);
  not not_4 (not_4_out, in_20);
  and and_1 (and_1_out, _0, not_1_out, not_1_out, not_3_out, not_4_out);
  and and_2 (and_2_out, _1, not_1_out, not_1_out, not_3_out, in_20);
  and and_3 (and_3_out, in_3, not_1_out, not_1_out, in_19, not_4_out);
  and and_4 (and_4_out, in_4, not_1_out, not_1_out, in_19, in_20);
  and and_5 (and_5_out, in_5, not_1_out, in_18, not_3_out, not_4_out);
  and and_6 (and_6_out, in_6, not_1_out, in_18, not_3_out, in_20);
  and and_7 (and_7_out, in_7, not_1_out, in_18, in_19, not_4_out);
  and and_8 (and_8_out, in_8, not_1_out, in_18, in_19, in_20);
  and and_9 (and_9_out, in_9, in_17, not_1_out, not_3_out, not_4_out);
  and and_10 (and_10_out, in_10, in_17, not_1_out, not_3_out, in_20);
  and and_11 (and_11_out, in_11, in_17, not_1_out, in_19, not_4_out);
  and and_12 (and_12_out, in_12, in_17, not_1_out, in_19, in_20);
  and and_13 (and_13_out, in_13, in_17, in_18, not_3_out, not_4_out);
  and and_14 (and_14_out, in_14, in_17, in_18, not_3_out, not_4_out);
  and and_15 (and_15_out, in_20, in_17, in_18, in_19, not_4_out);
  and and_16 (and_16_out, in_16, in_17, in_18, in_19, in_20);
  or or_1 (\выход , and_1_out, and_2_out, and_3_out, and_4_out, and_5_out, and_6_out, and_7_out, and_8_out, and_9_out, and_10_out, and_11_out, and_12_out, and_13_out, and_14_out, and_15_out, and_16_out);

  // Notes on the sheet:
  //   Кобяшова Д.А
  //   Мультиплексор
  //   управляющие входы
endmodule

module \Демультиплексор  (
  input  _1,
  input  in_2,
  input  in_3,
  input  in_4,
  input  in_5,
  output _0,
  output _1_2,
  output _2,
  output _3,
  output _4,
  output _5,
  output _6,
  output _7,
  output _8,
  output _9,
  output _10,
  output _11,
  output _12,
  output _13,
  output _14,
  output _15
);

  wire not_1_out, not_2_out, not_3_out, not_4_out;

  not not_1 (not_1_out, in_2);
  not not_2 (not_2_out, in_3);
  not not_3 (not_3_out, in_4);
  not not_4 (not_4_out, in_5);
  and and_1 (_0, _1, not_1_out, not_2_out, not_3_out, not_4_out);
  and and_2 (_1_2, _1, not_1_out, not_2_out, not_3_out, in_5);
  and and_3 (_2, _1, not_1_out, not_2_out, in_4, not_4_out);
  and and_4 (_3, _1, not_1_out, not_2_out, in_4, in_5);
  and and_5 (_4, _1, not_1_out, in_3, not_3_out, not_4_out);
  and and_6 (_5, _1, not_1_out, in_3, not_3_out, in_5);
  and and_7 (_6, _1, not_1_out, in_3, in_4, not_4_out);
  and and_8 (_7, _1, not_1_out, in_3, in_4, in_5);
  and and_9 (_8, _1, in_2, not_2_out, not_3_out, not_4_out);
  and and_10 (_9, _1, in_2, not_2_out, not_3_out, in_5);
  and and_11 (_10, _1, in_2, not_2_out, in_4, not_4_out);
  and and_12 (_11, _1, in_2, not_2_out, in_4, in_5);
  and and_13 (_12, _1, in_2, in_3, not_3_out, not_4_out);
  and and_14 (_13, _1, in_2, in_3, not_3_out, in_5);
  and and_15 (_14, _1, in_2, in_3, in_4, not_4_out);
  and and_16 (_15, _1, in_2, in_3, in_4, in_5);

  // Notes on the sheet:
  //   Кобяшова Д.А
  //   Демультиплексор
  //   управляющие входы
  //   выход
endmodule

module \Сдвиг  (
  input  in_1,
  input  in_2,
  input  in_3,
  input  in_4,
  input  in_5,
  input  in_6,
  input  in_7,
  input  in_8,
  input  \в ,
  output out_10,
  output out_11,
  output out_12,
  output out_13,
  output out_14,
  output out_15,
  output out_16,
  output out_17
);

  wire and_2_out, and_3_out, and_4_out, and_5_out, and_6_out, and_7_out, and_8_out, and_9_out, and_10_out,
       and_11_out, and_13_out, and_14_out, not_1_out;

  not not_1 (not_1_out, \в );
  and and_1 (out_10, not_1_out, in_2);
  and and_2 (and_2_out, in_1, \в );
  and and_3 (and_3_out, in_2, \в );
  and and_4 (and_4_out, not_1_out, in_3);
  and and_5 (and_5_out, in_3, \в );
  or or_1 (out_11, and_2_out, and_4_out);
  and and_6 (and_6_out, not_1_out, in_4);
  and and_7 (and_7_out, in_4, \в );
  or or_2 (out_12, and_3_out, and_6_out);
  or or_3 (out_13, and_5_out, and_8_out);
  and and_8 (and_8_out, not_1_out, in_5);
  or or_4 (out_14, and_7_out, and_10_out);
  and and_9 (and_9_out, in_5, \в );
  and and_10 (and_10_out, not_1_out, in_6);
  or or_5 (out_15, and_9_out, and_13_out);
  and and_11 (and_11_out, in_6, \в );
  or or_6 (out_16, and_11_out, and_14_out);
  and and_12 (out_17, in_7, \в );
  and and_13 (and_13_out, not_1_out, in_7);
  and and_14 (and_14_out, not_1_out, in_8);

  // Notes on the sheet:
  //   и
  //   г
  //   Кобяшова Д.А
  //   Схема сдвига
  //   выход
  //   входы
endmodule

module \Полусумматор  (
  input  in_1,
  input  in_2,
  output \результат ,
  output \перенос 
);

  wire and_1_out, and_2_out, not_1_out, not_2_out;

  not not_1 (not_1_out, in_2);
  not not_2 (not_2_out, in_1);
  and and_1 (and_1_out, in_1, not_1_out);
  and and_2 (and_2_out, not_2_out, in_2);
  and and_3 (\перенос , in_1, in_2);
  or or_1 (\результат , and_1_out, and_2_out);

  // Notes on the sheet:
  //   Кобяшова Д.А
  //   Полусумматор
endmodule

module \Полный_сумматор  (
  input  in_1,
  input  in_2,
  input  in_3,
  output out_4,
  output out_5
);

  wire and_1_out, and_2_out, and_3_out, and_4_out, and_5_out, and_6_out, not_1_out, not_2_out, not_3_out,
       not_4_out, or_1_out;

  not not_1 (not_1_out, in_3);
  not not_2 (not_2_out, in_2);
  and and_1 (and_1_out, in_2, not_1_out);
  and and_2 (and_2_out, not_2_out, in_3);
  and and_3 (and_3_out, in_2, in_3);
  or or_1 (or_1_out, and_1_out, and_2_out);
  and and_4 (and_4_out, in_1, not_3_out);
  not not_3 (not_3_out, or_1_out);
  not not_4 (not_4_out, in_1);
  and and_5 (and_5_out, not_4_out, or_1_out);
  and and_6 (and_6_out, in_1, or_1_out);
  or or_2 (out_5, and_6_out, and_3_out);
  or or_3 (out_4, and_4_out, and_5_out);
endmodule
