// Logisim project регистры с озу.circ as structural Verilog: 2 circuits, main circuit main
module main (
  input  \выбор_регистров ,
  input  [3:0] \адресный ,
  input  in_3
);

  wire clock_1_out, not_1_out, not_2_out;
  wire [7:0] controlled_buffer_1_out, controlled_buffer_2_out, controlled_buffer_3_out,
       controlled_buffer_4_out, ram_1_data, \регистр_Ё_2_q , \регистр_Ё_q ;

  Clock clock_1 (.out(clock_1_out));
  Register \u_регистр_Ё  (.D(controlled_buffer_2_out), .Q(\регистр_Ё_q ), .clr(clock_1_out));  // open: en, clk
  assign controlled_buffer_1_out = not_1_out ? \регистр_Ё_q  : 8'bz;  // Controlled_Buffer controlled_buffer_1
  not not_1 (not_1_out, in_3);
  assign controlled_buffer_2_out = in_3 ? controlled_buffer_1_out : 8'bz;  // Controlled_Buffer controlled_buffer_2
  assign controlled_buffer_3_out = not_2_out ? \регистр_Ё_2_q  : 8'bz;  // Controlled_Buffer controlled_buffer_3
  Register \u_регистр_Ё_2  (.D(controlled_buffer_4_out), .Q(\регистр_Ё_2_q ), .clr(clock_1_out));  // open: en, clk
  not not_2 (not_2_out, in_3);
  RAM #(.addrWidth(4)) ram_1 (.addr(\адресный ), .data(ram_1_data), .clk(clock_1_out), .ld(in_3));  // open: sel, clr
  assign controlled_buffer_4_out = in_3 ? controlled_buffer_3_out : 8'bz;  // Controlled_Buffer controlled_buffer_4
  Demultiplexer #(.width(8)) demultiplexer_1 (
    .out0(controlled_buffer_1_out), .out1(controlled_buffer_3_out), .in(ram_1_data), .sel(\выбор_регистров ));  // open: en

  // Notes on the sheet:
  //   Кобяшова Д.А
  //   Взимодействие регистров с ОЗУ
  //   чтение/запись
  //   0 - чтение
  //   1 - запись 
endmodule

module \алу  (
);


  // Notes on the sheet:
  //   Кобяшова Д.А
  //   Взимодействие регистров с АЛУ
endmodule
