// Logisim project схема выборки и начало эвм.circ as structural Verilog
module \мультиплексор  (
  input  _0,
  input  _1,
  input  in_3,
  input  in_4,
  input  in_5,
  input  in_6,
  input  in_7,
  input  in_8,
  input  in_9,
  input  in_10,
  input  in_11,
  input  in_12,
  input  in_13,
  input  in_14,
  input  in_15,
  input  in_16,
  input  in_17,
  input  in_18,
  input  in_19,
  input  in_20,
  output \выход 
);

  wire and_1_out, and_2_out, and_3_out, and_4_out, and_5_out, and_6_out, and_7_out, and_8_out, and_9_out,
       and_10_out, and_11_out, and_12_out, and_13_out, and_14_out, and_15_out, and_16_out, not_1_out,
       not_3_out, not_4_out;

  not not_1 (not_1_out, in_17);
  not not_2 (not_1_out, in_18);
  not not_3 (not_3_out, in_19);
  not not_4 (not_4_out, in_20);
  and and_1 (and_1_out, _0, not_1_out, not_1_out, not_3_out, not_4_out);
  and and_2 (and_2_out, _1, not_1_out, not_1_out, not_3_out, in_20);
  and and_3 (and_3_out, in_3, not_1_out, not_1_out, in_19, not_4_out);
  and and_4 (and_4_out, in_4, not_1_out, not_1_out, in_19, in_20);
  and and_5 (and_5_out, in_5, not_1_out, in_18, not_3_out, not_4_out);
  and and_6 (and_6_out, in_6, not_1_out, in_18, not_3_out, in_20);
  and and_7 (and_7_out, in_7, not_1_out, in_18, in_19, not_4_out);
  and and_8 (and_8_out, in_8, not_1_out, in_18, in_19, in_20);
  and and_9 (and_9_out, in_9, in_17, not_1_out, not_3_out, not_4_out);
  and and_10 (and_10_out, in_10, in_17, not_1_out, not_3_out, in_20);
  and and_11 (and_11_out, in_11, in_17, not_1_out, in_19, not_4_out);
  and and_12 (and_12_out, in_12, in_17, not_1_out, in_19, in_20);
  and and_13 (and_13_out, in_13, in_17, in_18, not_3_out, not_4_out);
  and and_14 (and_14_out, in_14, in_17, in_18, not_3_out, not_4_out);
  and and_15 (and_15_out, in_15, in_17, in_18, in_19, not_4_out);
  and and_16 (and_16_out, in_16, in_17, in_18, in_19, in_20);
  or or_1 (\выход , and_1_out, and_2_out, and_3_out, and_4_out, and_5_out, and_6_out, and_7_out, and_8_out, and_9_out, and_10_out, and_11_out, and_12_out, and_13_out, and_14_out, and_15_out, and_16_out);

  // Notes on the sheet:
  //   Кобяшова Д.А
  //   Мультиплексор
  //   управляющие входы
endmodule

module \Демультиплексор  (
  input  _1,
  input  in_2,
  input  in_3,
  input  in_4,
  input  in_5,
  output _0,
  output _1_2,
  output _2,
  output _3,
  output _4,
  output _5,
  output _6,
  output _7,
  output _8,
  output _9,
  output _10,
  output _11,
  output _12,
  output _13,
  output _14,
  output _15
);

  wire not_1_out, not_2_out, not_3_out, not_4_out;

  not not_1 (not_1_out, in_2);
  not not_2 (not_2_out, in_3);
  not not_3 (not_3_out, in_4);
  not not_4 (not_4_out, in_5);
  and and_1 (_0, _1, not_1_out, not_2_out, not_3_out, not_4_out);
  and and_2 (_1_2, _1, not_1_out, not_2_out, not_3_out, in_5);
  and and_3 (_2, _1, not_1_out, not_2_out, in_4, not_4_out);
  and and_4 (_3, _1, not_1_out, not_2_out, in_4, in_5);
  and and_5 (_4, _1, not_1_out, in_3, not_3_out, not_4_out);
  and and_6 (_5, _1, not_1_out, in_3, not_3_out, in_5);
  and and_7 (_6, _1, not_1_out, in_3, in_4, not_4_out);
  and and_8 (_7, _1, not_1_out, in_3, in_4, in_5);
  and and_9 (_8, _1, in_2, not_2_out, not_3_out, not_4_out);
  and and_10 (_9, _1, in_2, not_2_out, not_3_out, in_5);
  and and_11 (_10, _1, in_2, not_2_out, in_4, not_4_out);
  and and_12 (_11, _1, in_2, not_2_out, in_4, in_5);
  and and_13 (_12, _1, in_2, in_3, not_3_out, not_4_out);
  and and_14 (_13, _1, in_2, in_3, not_3_out, in_5);
  and and_15 (_14, _1, in_2, in_3, in_4, not_4_out);
  and and_16 (_15, _1, in_2, in_3, in_4, in_5);

  // Notes on the sheet:
  //   Кобяшова Д.А
  //   Демультиплексор
  //   управляющие входы
  //   выход
endmodule

module \Сдвиг  (
  input  in_1,
  input  in_2,
  input  in_3,
  input  in_4,
  input  in_5,
  input  in_6,
  input  in_7,
  input  in_8,
  input  \в ,
  output out_10,
  output out_11,
  output out_12,
  output out_13,
  output out_14,
  output out_15,
  output out_16,
  output out_17
);

  wire and_2_out, and_3_out, and_4_out, and_5_out, and_6_out, and_7_out, and_8_out, and_9_out, and_10_out,
       and_11_out, and_13_out, and_14_out, not_1_out;

  not not_1 (not_1_out, \в );
  and and_1 (out_10, not_1_out, in_2);
  and and_2 (and_2_out, in_1, \в );
  and and_3 (and_3_out, in_2, \в );
  and and_4 (and_4_out, in_3, \в );
  and and_5 (and_5_out, not_1_out, in_3);
  or or_1 (out_11, and_2_out, and_5_out);
  and and_6 (and_6_out, in_4, \в );
  and and_7 (and_7_out, not_1_out, in_4);
  or or_2 (out_13, and_4_out, and_8_out);
  or or_3 (out_12, and_3_out, and_7_out);
  and and_8 (and_8_out, not_1_out, in_5);
  or or_4 (out_14, and_6_out, and_9_out);
  and and_9 (and_9_out, not_1_out, in_6);
  and and_10 (and_10_out, in_5, \в );
  or or_5 (out_15, and_10_out, and_13_out);
  and and_11 (and_11_out, in_6, \в );
  or or_6 (out_16, and_11_out, and_14_out);
  and and_12 (out_17, in_7, \в );
  and and_13 (and_13_out, not_1_out, in_7);
  and and_14 (and_14_out, not_1_out, in_8);

  // Notes on the sheet:
  //   и
  //   г
  //   Кобяшова Д.А
  //   Схема сдвига
  //   выход
  //   входы
endmodule

module \Полусумматор  (
  input  _0,
  input  _1,
  output \результат ,
  output \перенос 
);

  wire and_1_out, and_2_out, not_1_out, not_2_out;

  not not_1 (not_1_out, _1);
  not not_2 (not_2_out, _0);
  and and_1 (and_1_out, _0, not_1_out);
  and and_2 (and_2_out, not_2_out, _1);
  and and_3 (\перенос , _0, _1);
  or or_1 (\результат , and_1_out, and_2_out);

  // Notes on the sheet:
  //   Кобяшова Д.А
  //   Полусумматор
endmodule

module \Полный_сумматор  (
  input  \перенос ,
  input  _0,
  input  _1,
  output \выход ,
  output \перенос_2 
);

  wire and_1_out, and_2_out, and_3_out, and_4_out, and_5_out, and_6_out, not_1_out, not_2_out, not_3_out,
       not_4_out, or_1_out;

  not not_1 (not_1_out, _1);
  not not_2 (not_2_out, _0);
  and and_1 (and_1_out, _0, not_1_out);
  and and_2 (and_2_out, not_2_out, _1);
  and and_3 (and_3_out, _0, _1);
  or or_1 (or_1_out, and_1_out, and_2_out);
  and and_4 (and_4_out, \перенос , not_3_out);
  not not_3 (not_3_out, or_1_out);
  not not_4 (not_4_out, \перенос );
  and and_5 (and_5_out, not_4_out, or_1_out);
  and and_6 (and_6_out, \перенос , or_1_out);
  or or_2 (\перенос_2 , and_6_out, and_3_out);
  or or_3 (\выход , and_4_out, and_5_out);

  // Notes on the sheet:
  //   Кобяшова Д.А
  //   Сумматор
endmodule

module \_8разрядный_мультиплексор  (
  input  in_1,
  input  in_2,
  input  in_3,
  input  in_4,
  input  in_5,
  input  in_6,
  input  in_7,
  input  in_8,
  input  in_9,
  input  in_10,
  input  in_11,
  input  in_12,
  input  in_13,
  input  in_14,
  input  in_15,
  input  in_16
);
endmodule

module \_8_разрядный_мультиплексор_16  (
  input  [7:0] \вход_16 ,
  input  [7:0] \вход_15 ,
  input  [7:0] \вход_14 ,
  input  [7:0] \вход_13 ,
  input  [7:0] \вход_12 ,
  input  [7:0] \вход_11 ,
  input  [7:0] \вход_10 ,
  input  [7:0] \вход_9 ,
  input  [7:0] \вход_8 ,
  input  [7:0] \вход_7 ,
  input  [7:0] \вход_6 ,
  input  [7:0] \вход_5 ,
  input  [7:0] \вход_4 ,
  input  [7:0] \вход_3 ,
  input  [7:0] \вход_2 ,
  input  [7:0] \вход_1 ,
  output [7:0] \выход_1 
);

  \мультиплексор  \_0_разряд  (
    ._0(\вход_1 [0]), ._1(\вход_2 [0]), .in_3(\вход_3 [0]), .in_4(\вход_4 [0]), .in_5(\вход_5 [0]),
    .in_6(\вход_6 [0]), .in_7(\вход_7 [0]), .in_8(\вход_8 [0]), .in_9(\вход_9 [0]), .in_10(\вход_10 [0]),
    .in_11(\вход_11 [0]), .in_12(\вход_12 [0]), .in_13(\вход_13 [0]), .in_14(\вход_14 [0]),
    .in_15(\вход_15 [0]), .in_16(\вход_16 [0]), .\выход (\выход_1 [0]));  // open: in_17, in_18, in_19, in_20
  \мультиплексор  \_1_разряд  (
    ._0(\вход_1 [1]), ._1(\вход_2 [1]), .in_3(\вход_3 [1]), .in_4(\вход_4 [1]), .in_5(\вход_5 [1]),
    .in_6(\вход_6 [1]), .in_7(\вход_7 [1]), .in_8(\вход_8 [1]), .in_9(\вход_9 [1]), .in_10(\вход_10 [1]),
    .in_11(\вход_11 [1]), .in_12(\вход_12 [1]), .in_13(\вход_13 [1]), .in_14(\вход_14 [1]),
    .in_15(\вход_15 [1]), .in_16(\вход_16 [1]), .\выход (\выход_1 [1]));  // open: in_17, in_18, in_19, in_20
  \мультиплексор  \_2_разряд  (
    ._0(\вход_1 [2]), ._1(\вход_2 [2]), .in_3(\вход_3 [2]), .in_4(\вход_4 [2]), .in_5(\вход_5 [2]),
    .in_6(\вход_6 [2]), .in_7(\вход_7 [2]), .in_8(\вход_8 [2]), .in_9(\вход_9 [2]), .in_10(\вход_10 [2]),
    .in_11(\вход_11 [2]), .in_12(\вход_12 [2]), .in_13(\вход_13 [2]), .in_14(\вход_14 [2]),
    .in_15(\вход_15 [2]), .in_16(\вход_16 [2]), .\выход (\выход_1 [2]));  // open: in_17, in_18, in_19, in_20
  \мультиплексор  \_3_разряд  (
    ._0(\вход_1 [3]), ._1(\вход_2 [3]), .in_3(\вход_3 [3]), .in_4(\вход_4 [3]), .in_5(\вход_5 [3]),
    .in_6(\вход_6 [3]), .in_7(\вход_7 [3]), .in_8(\вход_8 [3]), .in_9(\вход_9 [3]), .in_10(\вход_10 [3]),
    .in_11(\вход_11 [3]), .in_12(\вход_12 [3]), .in_13(\вход_13 [3]), .in_14(\вход_14 [3]),
    .in_15(\вход_15 [3]), .in_16(\вход_16 [3]), .\выход (\выход_1 [3]));  // open: in_17, in_18, in_19, in_20
  \мультиплексор  \_4_разряд  (
    ._0(\вход_1 [4]), ._1(\вход_2 [4]), .in_3(\вход_3 [4]), .in_4(\вход_4 [4]), .in_5(\вход_5 [4]),
    .in_6(\вход_6 [4]), .in_7(\вход_7 [4]), .in_8(\вход_8 [4]), .in_9(\вход_9 [4]), .in_10(\вход_10 [4]),
    .in_11(\вход_11 [4]), .in_12(\вход_12 [4]), .in_13(\вход_13 [4]), .in_14(\вход_14 [4]),
    .in_15(\вход_15 [4]), .in_16(\вход_16 [4]), .\выход (\выход_1 [4]));  // open: in_17, in_18, in_19, in_20
  \мультиплексор  \_5_разряд  (
    ._0(\вход_1 [5]), ._1(\вход_2 [5]), .in_3(\вход_3 [5]), .in_4(\вход_4 [5]), .in_5(\вход_5 [5]),
    .in_6(\вход_6 [5]), .in_7(\вход_7 [5]), .in_8(\вход_8 [5]), .in_9(\вход_9 [5]), .in_10(\вход_10 [5]),
    .in_11(\вход_11 [5]), .in_12(\вход_12 [5]), .in_13(\вход_13 [5]), .in_14(\вход_14 [5]),
    .in_15(\вход_15 [5]), .in_16(\вход_16 [5]), .\выход (\выход_1 [5]));  // open: in_17, in_18, in_19, in_20
  \мультиплексор  \_6__разряд  (
    ._0(\вход_1 [6]), ._1(\вход_2 [6]), .in_3(\вход_3 [6]), .in_4(\вход_4 [6]), .in_5(\вход_5 [6]),
    .in_6(\вход_6 [6]), .in_7(\вход_7 [6]), .in_8(\вход_8 [6]), .in_9(\вход_9 [6]), .in_10(\вход_10 [6]),
    .in_11(\вход_11 [6]), .in_12(\вход_12 [6]), .in_13(\вход_13 [6]), .in_14(\вход_14 [6]),
    .in_15(\вход_15 [6]), .in_16(\вход_16 [6]), .\выход (\выход_1 [6]));  // open: in_17, in_18, in_19, in_20
  \мультиплексор  \_7_разряд  (
    ._0(\вход_1 [7]), ._1(\вход_2 [7]), .in_3(\вход_3 [7]), .in_4(\вход_4 [7]), .in_5(\вход_5 [7]),
    .in_6(\вход_6 [7]), .in_7(\вход_7 [7]), .in_8(\вход_8 [7]), .in_9(\вход_9 [7]), .in_10(\вход_10 [7]),
    .in_11(\вход_11 [7]), .in_12(\вход_12 [7]), .in_13(\вход_13 [7]), .in_14(\вход_14 [7]),
    .in_15(\вход_15 [7]), .in_16(\вход_16 [7]), .\выход (\выход_1 [7]));  // open: in_17, in_18, in_19, in_20
endmodule

module \компаратор  (
  input  in_1,
  input  in_2,
  input  in_3,
  input  in_4,
  input  _0,
  input  _1,
  output out_7,
  output \Выход 
);

  wire and_1_out, and_2_out, not_1_out, not_2_out, or_1_out, or_2_out, xor_1_out, xor_2_out;

  xor xor_1 (xor_1_out, in_1, in_3);
  xor xor_2 (xor_2_out, in_2, in_4);
  not not_1 (not_1_out, _1);
  and and_1 (and_1_out, not_1_out, _0);
  and and_2 (and_2_out, _1, not_2_out);
  not not_2 (not_2_out, _0);
  or or_1 (or_1_out, and_1_out, and_2_out);
  or or_2 (or_2_out, xor_1_out, xor_2_out);
  not not_3 (\Выход , or_1_out);
  not not_4 (out_7, or_2_out);

  // Notes on the sheet:
  //   Кобяшова Д.А
  //   Компаратор
endmodule

module \СХЕМА_ПАМЯТИ  (
  input  \Сброс ,
  input  [3:0] in_2,
  input  [2:0] \Адрес ,
  output [3:0] out_4
);

  wire and_1_out, and_2_out, and_3_out, and_4_out, and_5_out, and_6_out, and_7_out, and_8_out, and_9_out,
       and_10_out, and_11_out, and_12_out, and_13_out, and_14_out, and_15_out, and_16_out, and_17_out,
       and_18_out, and_19_out, and_20_out, and_21_out, and_22_out, and_23_out, and_24_out, and_25_out,
       and_26_out, and_27_out, and_28_out, and_29_out, and_30_out, and_31_out, and_32_out, and_33_out,
       and_34_out, and_35_out, and_36_out, and_37_out, and_38_out, and_39_out, and_40_out, clock_1_out,
       d_ff_1_q, d_ff_2_q, d_ff_3_q, d_ff_4_q, d_ff_5_q, d_ff_6_q, d_ff_7_q, d_ff_8_q, d_ff_9_q, d_ff_10_q,
       d_ff_11_q, d_ff_12_q, d_ff_13_q, d_ff_14_q, d_ff_15_q, d_ff_16_q, d_ff_17_q, d_ff_18_q, d_ff_19_q,
       d_ff_20_q, d_ff_21_q, d_ff_22_q, d_ff_23_q, d_ff_24_q, d_ff_25_q, d_ff_26_q, d_ff_27_q, d_ff_28_q,
       d_ff_29_q, d_ff_30_q, d_ff_31_q, d_ff_32_q, decoder_1_out0, decoder_1_out1, decoder_1_out2,
       decoder_1_out3, decoder_1_out4, decoder_1_out5, decoder_1_out6, decoder_1_out7;

  Decoder #(.select(3)) decoder_1 (
    .out0(decoder_1_out0), .out1(decoder_1_out1), .out2(decoder_1_out2), .out3(decoder_1_out3),
    .out4(decoder_1_out4), .out5(decoder_1_out5), .out6(decoder_1_out6), .out7(decoder_1_out7), .sel(\Адрес ));  // open: en
  Clock clock_1 (.out(clock_1_out));
  and and_1 (and_1_out, clock_1_out, decoder_1_out0);
  and and_2 (and_2_out, clock_1_out, decoder_1_out1);
  and and_3 (and_3_out, clock_1_out, decoder_1_out2);
  and and_4 (and_4_out, clock_1_out, decoder_1_out3);
  and and_5 (and_5_out, clock_1_out, decoder_1_out4);
  and and_6 (and_6_out, clock_1_out, decoder_1_out5);
  and and_7 (and_7_out, clock_1_out, decoder_1_out6);
  and and_8 (and_8_out, clock_1_out, decoder_1_out7);
  D_Flip_Flop d_ff_1 (.clk(and_1_out), .D(in_2[3]), .Q(d_ff_1_q), .reset(\Сброс ));  // open: Qn, preset, en
  and and_9 (and_9_out, decoder_1_out0, d_ff_1_q);
  D_Flip_Flop d_ff_2 (.clk(and_2_out), .D(in_2[3]), .Q(d_ff_2_q), .reset(clock_1_out));  // open: Qn, preset, en
  D_Flip_Flop d_ff_3 (.clk(and_3_out), .D(in_2[3]), .Q(d_ff_3_q), .reset(clock_1_out));  // open: Qn, preset, en
  D_Flip_Flop d_ff_4 (.clk(and_4_out), .D(in_2[3]), .Q(d_ff_4_q), .reset(clock_1_out));  // open: Qn, preset, en
  D_Flip_Flop d_ff_5 (.clk(and_5_out), .D(in_2[3]), .Q(d_ff_5_q), .reset(clock_1_out));  // open: Qn, preset, en
  D_Flip_Flop d_ff_6 (.clk(and_6_out), .D(in_2[3]), .Q(d_ff_6_q), .reset(clock_1_out));  // open: Qn, preset, en
  D_Flip_Flop d_ff_7 (.clk(and_7_out), .D(in_2[3]), .Q(d_ff_7_q), .reset(clock_1_out));  // open: Qn, preset, en
  D_Flip_Flop d_ff_8 (.clk(and_8_out), .D(in_2[3]), .Q(d_ff_8_q), .reset(\Сброс ));  // open: Qn, preset, en
  and and_10 (and_10_out, decoder_1_out1, d_ff_2_q);
  and and_11 (and_11_out, decoder_1_out2, d_ff_3_q);
  and and_12 (and_12_out, decoder_1_out3, d_ff_4_q);
  and and_13 (and_13_out, decoder_1_out4, d_ff_5_q);
  and and_14 (and_14_out, decoder_1_out5, d_ff_6_q);
  and and_15 (and_15_out, decoder_1_out6, d_ff_7_q);
  and and_16 (and_16_out, decoder_1_out7, d_ff_8_q);
  or or_1 (out_4[3], and_16_out, and_15_out, and_14_out, and_13_out, and_12_out, and_11_out, and_10_out, and_9_out);
  D_Flip_Flop d_ff_9 (.clk(and_1_out), .D(in_2[2]), .Q(d_ff_9_q), .reset(\Сброс ));  // open: Qn, preset, en
  and and_17 (and_17_out, decoder_1_out0, d_ff_9_q);
  D_Flip_Flop d_ff_10 (.clk(and_2_out), .D(in_2[2]), .Q(d_ff_10_q), .reset(clock_1_out));  // open: Qn, preset, en
  and and_18 (and_18_out, decoder_1_out1, d_ff_10_q);
  D_Flip_Flop d_ff_11 (.clk(and_3_out), .D(in_2[2]), .Q(d_ff_11_q), .reset(clock_1_out));  // open: Qn, preset, en
  D_Flip_Flop d_ff_12 (.clk(and_4_out), .D(in_2[2]), .Q(d_ff_12_q), .reset(clock_1_out));  // open: Qn, preset, en
  and and_19 (and_19_out, decoder_1_out3, d_ff_12_q);
  D_Flip_Flop d_ff_13 (.clk(and_5_out), .D(and_5_out), .Q(d_ff_13_q), .reset(clock_1_out));  // open: Qn, preset, en
  and and_20 (and_20_out, decoder_1_out4, d_ff_13_q);
  D_Flip_Flop d_ff_14 (.clk(and_6_out), .D(in_2[2]), .Q(d_ff_14_q), .reset(clock_1_out));  // open: Qn, preset, en
  D_Flip_Flop d_ff_15 (.clk(and_7_out), .D(and_7_out), .Q(d_ff_15_q), .reset(clock_1_out));  // open: Qn, preset, en
  and and_21 (and_21_out, decoder_1_out6, d_ff_15_q);
  D_Flip_Flop d_ff_16 (.clk(and_8_out), .D(in_2[2]), .Q(d_ff_16_q), .reset(\Сброс ));  // open: Qn, preset, en
  and and_22 (and_22_out, decoder_1_out7, d_ff_16_q);
  and and_23 (and_23_out, decoder_1_out2, d_ff_11_q);
  and and_24 (and_24_out, decoder_1_out5, d_ff_14_q);
  or or_2 (out_4[2], and_22_out, and_21_out, and_24_out, and_20_out, and_19_out, and_23_out, and_18_out, and_17_out);
  D_Flip_Flop d_ff_17 (.clk(and_1_out), .D(in_2[1]), .Q(d_ff_17_q), .reset(\Сброс ));  // open: Qn, preset, en
  and and_25 (and_25_out, decoder_1_out0, d_ff_17_q);
  D_Flip_Flop d_ff_18 (.clk(and_2_out), .D(in_2[1]), .Q(d_ff_18_q), .reset(clock_1_out));  // open: Qn, preset, en
  and and_26 (and_26_out, decoder_1_out1, d_ff_18_q);
  D_Flip_Flop d_ff_19 (.clk(and_3_out), .D(in_2[1]), .Q(d_ff_19_q), .reset(clock_1_out));  // open: Qn, preset, en
  and and_27 (and_27_out, decoder_1_out2, d_ff_19_q);
  D_Flip_Flop d_ff_20 (.clk(and_4_out), .D(in_2[1]), .Q(d_ff_20_q), .reset(clock_1_out));  // open: Qn, preset, en
  and and_28 (and_28_out, decoder_1_out3, d_ff_20_q);
  D_Flip_Flop d_ff_21 (.clk(and_5_out), .D(in_2[1]), .Q(d_ff_21_q), .reset(clock_1_out));  // open: Qn, preset, en
  and and_29 (and_29_out, decoder_1_out4, d_ff_21_q);
  D_Flip_Flop d_ff_22 (.clk(and_6_out), .D(in_2[1]), .Q(d_ff_22_q), .reset(clock_1_out));  // open: Qn, preset, en
  and and_30 (and_30_out, decoder_1_out5, d_ff_22_q);
  D_Flip_Flop d_ff_23 (.clk(and_7_out), .D(in_2[1]), .Q(d_ff_23_q), .reset(clock_1_out));  // open: Qn, preset, en
  and and_31 (and_31_out, decoder_1_out6, d_ff_23_q);
  D_Flip_Flop d_ff_24 (.clk(and_8_out), .D(in_2[1]), .Q(d_ff_24_q), .reset(\Сброс ));  // open: Qn, preset, en
  and and_32 (and_32_out, decoder_1_out7, d_ff_24_q);
  or or_3 (out_4[1], and_32_out, and_31_out, and_30_out, and_29_out, and_28_out, and_27_out, and_26_out, and_25_out);
  D_Flip_Flop d_ff_25 (.clk(and_1_out), .D(in_2[0]), .Q(d_ff_25_q), .reset(\Сброс ));  // open: Qn, preset, en
  and and_33 (and_33_out, decoder_1_out0, d_ff_25_q);
  D_Flip_Flop d_ff_26 (.clk(and_2_out), .D(in_2[0]), .Q(d_ff_26_q), .reset(clock_1_out));  // open: Qn, preset, en
  and and_34 (and_34_out, decoder_1_out1, d_ff_26_q);
  D_Flip_Flop d_ff_27 (.clk(and_3_out), .D(in_2[0]), .Q(d_ff_27_q), .reset(clock_1_out));  // open: Qn, preset, en
  D_Flip_Flop d_ff_28 (.clk(and_4_out), .D(in_2[0]), .Q(d_ff_28_q), .reset(clock_1_out));  // open: Qn, preset, en
  and and_35 (and_35_out, decoder_1_out3, d_ff_28_q);
  D_Flip_Flop d_ff_29 (.clk(and_5_out), .D(in_2[0]), .Q(d_ff_29_q), .reset(clock_1_out));  // open: Qn, preset, en
  and and_36 (and_36_out, decoder_1_out4, d_ff_29_q);
  D_Flip_Flop d_ff_30 (.clk(and_6_out), .D(in_2[0]), .Q(d_ff_30_q), .reset(clock_1_out));  // open: Qn, preset, en
  D_Flip_Flop d_ff_31 (.clk(and_7_out), .D(in_2[0]), .Q(d_ff_31_q), .reset(clock_1_out));  // open: Qn, preset, en
  and and_37 (and_37_out, decoder_1_out6, d_ff_31_q);
  D_Flip_Flop d_ff_32 (.clk(and_8_out), .D(in_2[0]), .Q(d_ff_32_q), .reset(\Сброс ));  // open: Qn, preset, en
  and and_38 (and_38_out, decoder_1_out7, d_ff_32_q);
  and and_39 (and_39_out, decoder_1_out2, d_ff_27_q);
  and and_40 (and_40_out, decoder_1_out5, d_ff_30_q);
  or or_4 (out_4[0], and_38_out, and_37_out, and_40_out, and_36_out, and_35_out, and_39_out, and_34_out, and_33_out);

  // Notes on the sheet:
  //   Кобяшова Д.А
  //   Схема памяти
  //   Данные для записи
  //   Чтение данных
endmodule

module \алу_нач  (
  input  [7:0] _1,
  input  [7:0] _2,
  input  \перенос ,
  input  [2:0] \выбор ,
  output out_5
);

  wire adder_1_cout, adder_2_cout, subtractor_1_bout, subtractor_2_bout, undriven;
  wire [7:0] adder_1_out, adder_2_out, and_1_out, multiplexer_1_out, or_1_out, subtractor_1_out,
       subtractor_2_out, xor_1_out;

  Adder adder_1 (.a(_1), .b(_2), .out(adder_1_out), .cout(adder_1_cout));  // open: cin
  assign or_1_out = _1 | _2;  // OR_Gate or_1, 8 bits wide
  Adder adder_2 (.a(_1), .b(_2), .out(adder_2_out), .cin(\перенос ), .cout(adder_2_cout));
  Subtractor subtractor_1 (.a(_1), .b(_2), .out(subtractor_1_out), .bin(\перенос ), .bout(subtractor_1_bout));
  assign and_1_out = _1 & _2;  // AND_Gate and_1, 8 bits wide
  Subtractor subtractor_2 (.a(_1), .b(_2), .out(subtractor_2_out), .bin(\перенос ), .bout(subtractor_2_bout));
  assign xor_1_out = _1 ^ _2;  // XOR_Gate xor_1, 8 bits wide
  Multiplexer #(.select(3), .width(8)) multiplexer_1 (
    .in0(adder_1_out), .in1(or_1_out), .in2(adder_2_out), .in3(subtractor_1_out), .in4(and_1_out),
    .in5(subtractor_2_out), .in6(xor_1_out), .in7(subtractor_2_out), .out(multiplexer_1_out), .sel(\выбор ));  // open: en
  Multiplexer #(.select(3)) multiplexer_2 (
    .in0(adder_1_cout), .in1(undriven), .in2(adder_2_cout), .in3(subtractor_1_bout), .in4(undriven),
    .in5(subtractor_2_bout), .in6(undriven), .in7(subtractor_2_bout), .out(out_5), .sel(\выбор ));  // open: en
  Demultiplexer #(.width(8)) demultiplexer_1 ();  // open: out0, out1, in, sel, en

  // Notes on the sheet:
  //   +с переносом
  //   искл или
  //   сумматор
  //   или
  //   - с переносом
  //   и
  //   0
  //   1
  //   2
  //   3
  //   4
  //   5,7
  //   6
endmodule

module \АЛУ_нов  (
  input  [7:0] _0,
  input  [7:0] _1,
  input  [2:0] \выбор ,
  output [7:0] \выход 
);

  wire [7:0] \n8_1_выход , \и_8_1_выход , \или_8_1_выход , \компаратор_8_1_out_3 , \сдвиг_8_1_выход ,
       \сдвиг_8_2_выход , \сдвие_8_1_1_выход , \сдвие_8_1_2_выход ;

  \и_8  \u_и_8_1  (._0(_0), ._1(_1), .\Выход (\и_8_1_выход ));
  \или_8  \u_или_8_1  (._0(_0), ._1(_1), .\Выход (\или_8_1_выход ));
  \сдвиг_8  \u_сдвиг_8_1  (.\вход (_0), .\выход (\сдвиг_8_1_выход ));  // open: сдвиг
  \сдвие_8_1  \u_сдвие_8_1_1  (.\вход (_0), .\выход (\сдвие_8_1_1_выход ));  // open: сдвиг
  \сдвиг_8  \u_сдвиг_8_2  (.\вход (_1), .\выход (\сдвиг_8_2_выход ));  // open: сдвиг
  \сдвие_8_1  \u_сдвие_8_1_2  (.\вход (_1), .\выход (\сдвие_8_1_2_выход ));  // open: сдвиг
  _8 u_8_1 (._0(_0), ._1(_1), .\выход (\n8_1_выход ));
  \компаратор_8  \u_компаратор_8_1  (.in_1(_0), .in_2(_1), .out_3(\компаратор_8_1_out_3 ));
  Multiplexer #(.select(3), .width(8)) multiplexer_1 (
    .in0(\и_8_1_выход ), .in1(\или_8_1_выход ), .in2(\сдвиг_8_1_выход ), .in3(\сдвие_8_1_1_выход ),
    .in4(\сдвиг_8_2_выход ), .in5(\сдвие_8_1_2_выход ), .in6(\n8_1_выход ), .in7(\компаратор_8_1_out_3 ),
    .out(\выход ), .sel(\выбор ));  // open: en

  // Notes on the sheet:
  //   Кобяшова Д.А
  //   АЛУ
  //   номер бита соответсвтует номеру операции, 
  //   которая выполнится и придет на мультиплексор
  //   и
  //   или
  //   сдвиг влево
  //   1(0)  число
  //   1(0)  число
  //   сдвиг вправо
  //   сдвиг влево
  //   2 (1)  число
  //   сдвиг вправо
  //   сумматор
  //   компаратор
  //   2 (1)  число
endmodule

module \или_8  (
  input  [7:0] _0,
  input  [7:0] _1,
  output [7:0] \Выход 
);

  or or_1 (\Выход [0], _0[0], _1[0]);
  or or_2 (\Выход [1], _0[1], _1[1]);
  or or_3 (\Выход [2], _0[2], _1[2]);
  or or_4 (\Выход [3], _0[3], _1[3]);
  or or_5 (\Выход [4], _0[4], _1[4]);
  or or_6 (\Выход [5], _0[5], _1[5]);
  or or_7 (\Выход [6], _0[6], _1[6]);
  or or_8 (\Выход [7], _0[7], _1[7]);

  // Notes on the sheet:
  //   Кобяшова Д.А
  //   Побитовое или
endmodule

module \и_8  (
  input  [7:0] _0,
  input  [7:0] _1,
  output [7:0] \Выход 
);

  and and_1 (\Выход [0], _0[0], _1[0]);
  and and_2 (\Выход [1], _0[1], _1[1]);
  and and_3 (\Выход [2], _0[2], _1[2]);
  and and_4 (\Выход [3], _0[3], _1[3]);
  and and_5 (\Выход [4], _0[4], _1[4]);
  and and_6 (\Выход [5], _0[5], _1[5]);
  and and_7 (\Выход [6], _0[6], _1[6]);
  and and_8 (\Выход [7], _0[7], _1[7]);

  // Notes on the sheet:
  //   Кобяшова Д.А
  //   Побитовое и
endmodule

module _8 (
  input  [7:0] _0,
  input  [7:0] _1,
  output [7:0] \выход 
);

  wire \полный_сумматор_1_перенос_2 , \полный_сумматор_2_перенос_2 , \полный_сумматор_3_перенос_2 ,
       \полный_сумматор_4_перенос_2 , \полный_сумматор_5_перенос_2 , \полный_сумматор_6_перенос_2 ,
       \полусумматор_1_перенос ;

  \Полусумматор  \u_полусумматор_1  (
    ._0(_0[0]), ._1(_1[0]), .\результат (\выход [0]), .\перенос (\полусумматор_1_перенос ));
  \Полный_сумматор  \u_полный_сумматор_1  (
    ._0(_0[1]), ._1(_1[1]), .\перенос (\полусумматор_1_перенос ),
    .\перенос_2 (\полный_сумматор_1_перенос_2 ), .\выход (\выход [1]));
  \Полный_сумматор  \u_полный_сумматор_2  (
    ._0(_0[2]), ._1(_1[2]), .\перенос (\полный_сумматор_1_перенос_2 ),
    .\перенос_2 (\полный_сумматор_2_перенос_2 ), .\выход (\выход [2]));
  \Полный_сумматор  \u_полный_сумматор_3  (
    ._0(_0[3]), ._1(_1[3]), .\перенос (\полный_сумматор_2_перенос_2 ),
    .\перенос_2 (\полный_сумматор_3_перенос_2 ), .\выход (\выход [3]));
  \Полный_сумматор  \u_полный_сумматор_4  (
    ._0(_0[4]), ._1(_1[4]), .\перенос (\полный_сумматор_3_перенос_2 ),
    .\перенос_2 (\полный_сумматор_4_перенос_2 ), .\выход (\выход [4]));
  \Полный_сумматор  \u_полный_сумматор_5  (
    ._0(_0[5]), ._1(_1[5]), .\перенос (\полный_сумматор_4_перенос_2 ),
    .\перенос_2 (\полный_сумматор_5_перенос_2 ), .\выход (\выход [5]));
  \Полный_сумматор  \u_полный_сумматор_6  (
    ._0(_0[6]), ._1(_1[6]), .\перенос (\полный_сумматор_5_перенос_2 ),
    .\перенос_2 (\полный_сумматор_6_перенос_2 ), .\выход (\выход [6]));
  \Полный_сумматор  \u_полный_сумматор_7  (
    ._0(_0[7]), ._1(_1[7]), .\перенос (\полный_сумматор_6_перенос_2 ), .\выход (\выход [7]));  // open: перенос_2

  // Notes on the sheet:
  //   Кобяшова Д.А
  //   Сумматор
endmodule

module \сдвиг_8  (
  input  [7:0] \вход ,
  input  \сдвиг ,
  output [7:0] \выход 
);

  wire and_1_out, and_2_out, and_3_out, and_4_out, and_5_out, and_6_out, and_7_out, and_8_out, and_9_out,
       and_10_out, and_11_out, and_12_out, and_13_out, and_14_out, and_15_out, and_16_out, and_17_out,
       and_18_out, and_19_out, and_20_out, and_21_out, and_22_out, and_23_out, and_24_out, not_1_out,
       not_2_out, not_3_out, not_4_out, not_5_out, not_6_out, not_7_out, not_8_out, not_9_out, not_10_out,
       not_11_out, not_12_out, not_13_out, not_14_out, not_15_out, not_16_out, not_17_out, not_18_out,
       not_19_out, not_20_out, not_21_out, not_22_out, not_23_out, not_24_out, not_25_out;

  not not_1 (not_1_out, \вход [3]);
  and and_1 (and_1_out, not_1_out, \вход [1], not_2_out);
  not not_2 (not_2_out, \сдвиг );
  not not_3 (not_3_out, \вход [1]);
  and and_2 (and_2_out, \вход [3], not_3_out, \сдвиг );
  and and_3 (and_3_out, \вход [3], \вход [1], not_4_out);
  not not_4 (not_4_out, \сдвиг );
  and and_4 (and_4_out, \вход [3], \вход [1], \сдвиг );
  not not_5 (not_5_out, \вход [6]);
  and and_5 (and_5_out, not_5_out, \вход [4], not_6_out);
  not not_6 (not_6_out, \сдвиг );
  not not_7 (not_7_out, \вход [4]);
  and and_6 (and_6_out, \вход [6], not_7_out, \сдвиг );
  and and_7 (and_7_out, \вход [6], \вход [4], not_8_out);
  not not_8 (not_8_out, \сдвиг );
  and and_8 (and_8_out, \вход [6], \вход [4], \сдвиг );
  or or_1 (\выход [2], and_1_out, and_2_out, and_3_out, and_4_out);
  or or_2 (\выход [5], and_5_out, and_6_out, and_7_out, and_8_out);
  not not_9 (not_9_out, \вход [4]);
  not not_10 (not_10_out, \сдвиг );
  not not_11 (not_11_out, \вход [2]);
  not not_12 (not_12_out, \сдвиг );
  not not_13 (not_13_out, \вход [7]);
  not not_14 (not_14_out, \сдвиг );
  not not_15 (not_15_out, \вход [5]);
  not not_16 (not_16_out, \сдвиг );
  not not_17 (not_17_out, \вход [2]);
  and and_9 (and_9_out, not_17_out, \вход [0], not_18_out);
  not not_18 (not_18_out, \сдвиг );
  not not_19 (not_19_out, \вход [0]);
  and and_10 (and_10_out, \вход [2], not_19_out, \сдвиг );
  and and_11 (and_11_out, \вход [2], \вход [0], not_20_out);
  not not_20 (not_20_out, \сдвиг );
  and and_12 (and_12_out, \вход [2], \вход [0], \сдвиг );
  and and_13 (and_13_out, not_9_out, \вход [2], not_10_out);
  and and_14 (and_14_out, \вход [4], not_11_out, \сдвиг );
  and and_15 (and_15_out, \вход [2], \вход [2], not_12_out);
  and and_16 (and_16_out, \вход [4], \вход [2], \сдвиг );
  not not_21 (not_21_out, \вход [5]);
  and and_17 (and_17_out, not_21_out, \вход [3], not_22_out);
  not not_22 (not_22_out, \сдвиг );
  and and_18 (and_18_out, \вход [5], not_23_out, \сдвиг );
  not not_23 (not_23_out, \вход [3]);
  and and_19 (and_19_out, \вход [5], \вход [3], not_24_out);
  not not_24 (not_24_out, \сдвиг );
  and and_20 (and_20_out, \вход [5], \вход [3], \сдвиг );
  and and_21 (and_21_out, not_13_out, \вход [5], not_14_out);
  and and_22 (and_22_out, \вход [7], not_15_out, \сдвиг );
  and and_23 (and_23_out, \вход [7], \вход [5], not_16_out);
  and and_24 (and_24_out, \вход [7], \вход [5], \сдвиг );
  or or_3 (\выход [1], and_9_out, and_10_out, and_11_out, and_12_out);
  or or_4 (\выход [3], and_13_out, and_14_out, and_15_out, and_16_out);
  or or_5 (\выход [4], and_17_out, and_18_out, and_19_out, and_20_out);
  or or_6 (\выход [6], and_21_out, and_22_out, and_23_out, and_24_out);
  not not_25 (not_25_out, \сдвиг );
  and and_25 (\выход [0], \вход [1], \сдвиг );
  and and_26 (\выход [7], not_25_out, \вход [6]);

  // Notes on the sheet:
  //   Кобяшова Д.А
  //   Схема сдвига
endmodule

module \компаратор_8  (
  input  [7:0] in_1,
  input  [7:0] in_2,
  output [7:0] out_3
);

  wire \компоратор_20_1_выход , \компоратор_20_2_выход , \компоратор_20_3_выход , \компоратор_20_4_выход ,
       \компоратор_20_5_выход , \компоратор_20_6_выход , \компоратор_20_7_выход , \компоратор_20_8_выход ;

  \компоратор_20  \u_компоратор_20_1  (._0(in_1[0]), ._1(in_2[0]), .\Выход (\компоратор_20_1_выход ));
  \компоратор_20  \u_компоратор_20_2  (._0(in_1[1]), ._1(in_2[1]), .\Выход (\компоратор_20_2_выход ));
  \компоратор_20  \u_компоратор_20_3  (._0(in_1[2]), ._1(in_2[2]), .\Выход (\компоратор_20_3_выход ));
  \компоратор_20  \u_компоратор_20_4  (._0(in_1[3]), ._1(in_2[3]), .\Выход (\компоратор_20_4_выход ));
  \компоратор_20  \u_компоратор_20_5  (._0(in_1[4]), ._1(in_2[4]), .\Выход (\компоратор_20_5_выход ));
  \компоратор_20  \u_компоратор_20_6  (._0(in_1[5]), ._1(in_2[5]), .\Выход (\компоратор_20_6_выход ));
  \компоратор_20  \u_компоратор_20_7  (._0(in_1[6]), ._1(in_2[6]), .\Выход (\компоратор_20_7_выход ));
  \компоратор_20  \u_компоратор_20_8  (._0(in_1[7]), ._1(in_2[7]), .\Выход (\компоратор_20_8_выход ));
  and and_1 (out_3[0], \компоратор_20_1_выход , \компоратор_20_2_выход , \компоратор_20_3_выход , \компоратор_20_4_выход , \компоратор_20_5_выход , \компоратор_20_6_выход , \компоратор_20_7_выход , \компоратор_20_8_выход );

  assign out_3[7:1] = {7{1'b0}};

  // Notes on the sheet:
  //   Кобяшова Д.А
  //   Компаратор
endmodule

module \компоратор_20  (
  input  _0,
  input  _1,
  output \Выход 
);

  wire and_1_out, and_2_out, not_1_out, not_2_out, or_1_out;

  not not_1 (not_1_out, _1);
  not not_2 (not_2_out, _0);
  and and_1 (and_1_out, not_1_out, _0);
  and and_2 (and_2_out, _1, not_2_out);
  or or_1 (or_1_out, and_1_out, and_2_out);
  not not_3 (\Выход , or_1_out);

  // Notes on the sheet:
  //   Кобяшова Д.А
  //   Компаратор
endmodule

module \сдвие_8_1  (
  input  [7:0] \вход ,
  input  \сдвиг ,
  output [7:0] \выход 
);

  wire and_1_out, and_2_out, and_3_out, and_4_out, and_5_out, and_6_out, and_7_out, and_8_out, and_9_out,
       and_10_out, and_11_out, and_12_out, and_13_out, and_14_out, and_15_out, and_16_out, and_17_out,
       and_18_out, and_19_out, and_20_out, and_21_out, and_22_out, and_23_out, and_24_out, not_1_out,
       not_2_out, not_3_out, not_4_out, not_5_out, not_6_out, not_7_out, not_8_out, not_9_out, not_10_out,
       not_11_out, not_12_out, not_13_out, not_14_out, not_15_out, not_16_out, not_17_out, not_18_out,
       not_19_out, not_20_out, not_21_out, not_22_out, not_23_out, not_24_out, not_25_out;

  not not_1 (not_1_out, \вход [3]);
  and and_1 (and_1_out, not_1_out, \вход [1], not_2_out);
  not not_2 (not_2_out, \сдвиг );
  and and_2 (and_2_out, \вход [3], not_3_out, \сдвиг );
  not not_3 (not_3_out, \вход [1]);
  and and_3 (and_3_out, \вход [3], \вход [1], not_4_out);
  not not_4 (not_4_out, \сдвиг );
  and and_4 (and_4_out, \вход [3], \вход [1], \сдвиг );
  not not_5 (not_5_out, \вход [6]);
  and and_5 (and_5_out, not_5_out, \вход [4], not_6_out);
  not not_6 (not_6_out, \сдвиг );
  not not_7 (not_7_out, \вход [4]);
  and and_6 (and_6_out, \вход [6], not_7_out, \сдвиг );
  and and_7 (and_7_out, \вход [6], \вход [4], not_8_out);
  not not_8 (not_8_out, \сдвиг );
  and and_8 (and_8_out, \вход [6], \вход [4], \сдвиг );
  or or_1 (\выход [2], and_1_out, and_2_out, and_3_out, and_4_out);
  or or_2 (\выход [5], and_5_out, and_6_out, and_7_out, and_8_out);
  not not_9 (not_9_out, \вход [4]);
  not not_10 (not_10_out, \сдвиг );
  not not_11 (not_11_out, \вход [2]);
  not not_12 (not_12_out, \сдвиг );
  not not_13 (not_13_out, \вход [7]);
  not not_14 (not_14_out, \сдвиг );
  not not_15 (not_15_out, \вход [5]);
  not not_16 (not_16_out, \сдвиг );
  not not_17 (not_17_out, \вход [2]);
  and and_9 (and_9_out, not_17_out, \вход [0], not_18_out);
  not not_18 (not_18_out, \сдвиг );
  and and_10 (and_10_out, \вход [2], not_19_out, \сдвиг );
  not not_19 (not_19_out, \вход [0]);
  and and_11 (and_11_out, \вход [2], \вход [0], not_20_out);
  not not_20 (not_20_out, \сдвиг );
  and and_12 (and_12_out, \вход [2], \вход [0], \сдвиг );
  and and_13 (and_13_out, not_9_out, \вход [2], not_10_out);
  and and_14 (and_14_out, \вход [4], not_11_out, \сдвиг );
  and and_15 (and_15_out, \вход [2], \вход [2], not_12_out);
  and and_16 (and_16_out, \вход [4], \вход [2], \сдвиг );
  not not_21 (not_21_out, \вход [5]);
  and and_17 (and_17_out, not_21_out, \вход [3], not_22_out);
  not not_22 (not_22_out, \сдвиг );
  not not_23 (not_23_out, \вход [3]);
  and and_18 (and_18_out, \вход [5], not_23_out, \сдвиг );
  and and_19 (and_19_out, \вход [5], \вход [3], not_24_out);
  not not_24 (not_24_out, \сдвиг );
  and and_20 (and_20_out, \вход [5], \вход [3], \сдвиг );
  and and_21 (and_21_out, not_13_out, \вход [5], not_14_out);
  and and_22 (and_22_out, \вход [7], not_15_out, \сдвиг );
  and and_23 (and_23_out, \вход [7], \вход [5], not_16_out);
  and and_24 (and_24_out, \вход [7], \вход [5], \сдвиг );
  or or_3 (\выход [1], and_9_out, and_10_out, and_11_out, and_12_out);
  or or_4 (\выход [3], and_13_out, and_14_out, and_15_out, and_16_out);
  or or_5 (\выход [4], and_17_out, and_18_out, and_19_out, and_20_out);
  or or_6 (\выход [6], and_21_out, and_22_out, and_23_out, and_24_out);
  not not_25 (not_25_out, \сдвиг );
  and and_25 (\выход [0], \вход [1], \сдвиг );
  and and_26 (\выход [7], not_25_out, \вход [6]);

  // Notes on the sheet:
  //   Кобяшова Д.А
  //   Схема сдвига
endmodule

module \АЛУ_КОНЕЧНЫЙ  (
  input  [7:0] _0,
  input  [7:0] _1,
  input  [2:0] \выбор ,
  output [7:0] \выход 
);

  wire [7:0] \n8_1_выход , \и_8_1_выход , \или_8_1_выход , \компаратор_8_1_out_3 , \сдвиг_8_1_выход ,
       \сдвиг_8_2_выход , \сдвие_8_1_1_выход , \сдвие_8_1_2_выход ;

  \и_8  \u_и_8_1  (._0(_0), ._1(_1), .\Выход (\и_8_1_выход ));
  \или_8  \u_или_8_1  (._0(_0), ._1(_1), .\Выход (\или_8_1_выход ));
  \сдвиг_8  \u_сдвиг_8_1  (.\вход (_0), .\выход (\сдвиг_8_1_выход ));  // open: сдвиг
  \сдвие_8_1  \u_сдвие_8_1_1  (.\вход (_0), .\выход (\сдвие_8_1_1_выход ));  // open: сдвиг
  \сдвиг_8  \u_сдвиг_8_2  (.\вход (_1), .\выход (\сдвиг_8_2_выход ));  // open: сдвиг
  \сдвие_8_1  \u_сдвие_8_1_2  (.\вход (_1), .\выход (\сдвие_8_1_2_выход ));  // open: сдвиг
  _8 u_8_1 (._0(_0), ._1(_1), .\выход (\n8_1_выход ));
  \компаратор_8  \u_компаратор_8_1  (.in_1(_0), .in_2(_1), .out_3(\компаратор_8_1_out_3 ));
  Multiplexer #(.select(3), .width(8)) multiplexer_1 (
    .in0(\и_8_1_выход ), .in1(\или_8_1_выход ), .in2(\сдвиг_8_1_выход ), .in3(\сдвие_8_1_1_выход ),
    .in4(\сдвиг_8_2_выход ), .in5(\сдвие_8_1_2_выход ), .in6(\n8_1_выход ), .in7(\компаратор_8_1_out_3 ),
    .out(\выход ), .sel(\выбор ));  // open: en

  // Notes on the sheet:
  //   Кобяшова Д.А
  //   АЛУ
  //   номер бита соответсвтует номеру операции, 
  //   которая выполнится и придет на мультиплексор
  //   и
  //   или
  //   сдвиг влево
  //   1(0)  число
  //   1(0)  число
  //   сдвиг вправо
  //   сдвиг влево
  //   2 (1)  число
  //   сдвиг вправо
  //   сумматор
  //   компаратор
  //   2 (1)  число
endmodule

module \буферы  (
  input  \выбор_регистров ,
  input  [3:0] \адресный ,
  input  in_3
);

  wire clock_1_out, not_1_out, not_2_out;
  wire [7:0] controlled_buffer_1_out, controlled_buffer_2_out, controlled_buffer_3_out,
       controlled_buffer_4_out, ram_1_data, \регистр_Ё_2_q , \регистр_Ё_q ;

  Clock clock_1 (.out(clock_1_out));
  Register \u_регистр_Ё  (.D(controlled_buffer_2_out), .Q(\регистр_Ё_q ), .clr(clock_1_out));  // open: en, clk
  assign controlled_buffer_1_out = not_1_out ? \регистр_Ё_q  : 8'bz;  // Controlled_Buffer controlled_buffer_1
  not not_1 (not_1_out, in_3);
  assign controlled_buffer_2_out = in_3 ? controlled_buffer_1_out : 8'bz;  // Controlled_Buffer controlled_buffer_2
  Register \u_регистр_Ё_2  (.D(controlled_buffer_4_out), .Q(\регистр_Ё_2_q ), .clr(clock_1_out));  // open: en, clk
  assign controlled_buffer_3_out = not_2_out ? \регистр_Ё_2_q  : 8'bz;  // Controlled_Buffer controlled_buffer_3
  not not_2 (not_2_out, in_3);
  RAM #(.addrWidth(4)) ram_1 (.addr(\адресный ), .data(ram_1_data), .clk(clock_1_out), .ld(in_3));  // open: sel, clr
  assign controlled_buffer_4_out = in_3 ? controlled_buffer_3_out : 8'bz;  // Controlled_Buffer controlled_buffer_4
  Demultiplexer #(.width(8)) demultiplexer_1 (
    .out0(controlled_buffer_1_out), .out1(controlled_buffer_3_out), .in(ram_1_data), .sel(\выбор_регистров ));  // open: en

  // Notes on the sheet:
  //   Кобяшова Д.А
  //   Взимодействие регистров с ОЗУ
  //   чтение/запись
  //   0 - чтение
  //   1 - запись 
endmodule

module \регистры_с_алу  (
  input  \выбор_регистров ,
  input  \память ,
  input  [2:0] \выбор_операции ,
  input  [3:0] \адресный ,
  input  in_5
);

  wire clock_1_out, not_1_out, not_2_out, not_3_out;
  wire [7:0] controlled_buffer_1_out, controlled_buffer_2_out, controlled_buffer_3_out,
       controlled_buffer_4_out, ram_1_data, \алу_конечный_1_выход , \регистр_Ё_2_q , \регистр_Ё_q ;

  Clock clock_1 (.out(clock_1_out));
  Register \u_регистр_Ё  (.D(controlled_buffer_2_out), .Q(\регистр_Ё_q ), .clr(clock_1_out));  // open: en, clk
  assign controlled_buffer_1_out = not_1_out ? \регистр_Ё_q  : 8'bz;  // Controlled_Buffer controlled_buffer_1
  not not_1 (not_1_out, in_5);
  assign controlled_buffer_2_out = in_5 ? controlled_buffer_1_out : 8'bz;  // Controlled_Buffer controlled_buffer_2
  assign controlled_buffer_3_out = not_2_out ? \регистр_Ё_2_q  : 8'bz;  // Controlled_Buffer controlled_buffer_3
  Register \u_регистр_Ё_2  (.D(controlled_buffer_4_out), .Q(\регистр_Ё_2_q ), .clr(clock_1_out));  // open: en, clk
  not not_2 (not_2_out, in_5);
  RAM #(.addrWidth(4)) ram_1 (
    .addr(\адресный ), .data(ram_1_data), .sel(\память ), .clk(clock_1_out), .ld(in_5));  // open: clr
  assign controlled_buffer_4_out = in_5 ? controlled_buffer_3_out : 8'bz;  // Controlled_Buffer controlled_buffer_4
  Demultiplexer #(.width(8)) demultiplexer_1 (
    .out0(controlled_buffer_1_out), .out1(controlled_buffer_3_out), .in(ram_1_data), .sel(\выбор_регистров ));  // open: en
  \АЛУ_КОНЕЧНЫЙ  \u_алу_конечный_1  (
    ._0(controlled_buffer_3_out), ._1(\регистр_Ё_q ), .\выбор (\выбор_операции ),
    .\выход (\алу_конечный_1_выход ));
  assign controlled_buffer_4_out = not_3_out ? \алу_конечный_1_выход  : 8'bz;  // Controlled_Buffer controlled_buffer_5
  not not_3 (not_3_out, \память );

  // Notes on the sheet:
  //   000 - или
  //   001 - и
  //   Кобяшова Д.А
  //   Взимодействие регистров с АЛУ
  //   010 - число 1, сдвиг влево
  //   011 - число 1, сдвиг вправо
  //   100 - число 2, сдвиг влево
  //   101 - число 2, сдвиг вправо
  //   110 - сравнение
  //   111 - сложение 
  //   чтение/запись
  //   0 - чтение
  //   1 - запись 
  //   выбор
  //   выход
endmodule

module \схема_1  (
  input  [7:0] \адрес_для_перехода ,
  output [5:0] \код_действия ,
  output [5:0] \дополнительные_данные ,
  output [11:0] \инструкция_с_описаним_действий 
);

  wire clock_1_out;
  wire [7:0] \адрес_текущей_инструкции_q ;

  Adder adder_1 (.a(\адрес_текущей_инструкции_q ), .b(8'h1), .out(\адрес_для_перехода ));  // open: cin, cout
  Register \u_адрес_текущей_инструкции  (
    .D(\адрес_для_перехода ), .Q(\адрес_текущей_инструкции_q ), .clr(clock_1_out));  // open: en, clk
  Clock clock_1 (.out(clock_1_out));
  RAM #(.dataWidth(12)) ram_1 (
    .addr(\адрес_текущей_инструкции_q ),
    .data({\дополнительные_данные , \инструкция_с_описаним_действий [5:0]}));  // open: sel, clk, ld, clr

  assign \инструкция_с_описаним_действий [11:6] = \дополнительные_данные ;
  assign \код_действия  = \инструкция_с_описаним_действий [5:0];

  // Notes on the sheet:
  //   память с командами
endmodule

module \схема_выборки  (
  input  [7:0] \адрес_для_перехода ,
  input  \выбор_источника_след_инструкции ,
  output [11:0] \инструкция_с_описаним_действий ,
  output [3:0] \код_действия ,
  output [7:0] \дополнительные_данные 
);

  wire clock_1_out, not_1_out;
  wire [7:0] adder_1_out, controlled_buffer_1_out, \адрес_текущей_инструкции_q ;

  Adder adder_1 (.a(\адрес_текущей_инструкции_q ), .b(8'h1), .out(adder_1_out));  // open: cin, cout
  assign controlled_buffer_1_out = \выбор_источника_след_инструкции  ? adder_1_out : 8'bz;  // Controlled_Buffer controlled_buffer_1
  assign controlled_buffer_1_out = not_1_out ? \адрес_для_перехода  : 8'bz;  // Controlled_Buffer controlled_buffer_2
  Register \u_адрес_текущей_инструкции  (
    .D(controlled_buffer_1_out), .Q(\адрес_текущей_инструкции_q ), .clk(clock_1_out));  // open: en, clr
  Clock clock_1 (.out(clock_1_out));
  not not_1 (not_1_out, \выбор_источника_след_инструкции );
  RAM #(.dataWidth(12)) ram_1 (
    .addr(\адрес_текущей_инструкции_q ),
    .data({\дополнительные_данные , \инструкция_с_описаним_действий [3:0]}));  // open: sel, clk, ld, clr

  assign \инструкция_с_описаним_действий [11:4] = \дополнительные_данные ;
  assign \код_действия  = \инструкция_с_описаним_действий [3:0];

  // Notes on the sheet:
  //   память с командами
endmodule

module \мини_эвм  (
  input  [7:0] \адрес_для_перехода ,
  input  \выбор_источника_след_инструкции ,
  input  \выбор_регистров ,
  input  \память ,
  input  [2:0] \выбор_операции ,
  input  [3:0] \адресный ,
  input  in_7,
  output [11:0] \инструкция_с_описаним_действий ,
  output [3:0] \код_действия ,
  output [7:0] \дополнительные_данные 
);

  wire clock_1_out, clock_2_out, not_1_out, not_2_out, not_3_out, not_4_out;
  wire [7:0] adder_1_out, controlled_buffer_1_out, controlled_buffer_3_out, controlled_buffer_4_out,
       controlled_buffer_5_out, controlled_buffer_6_out, ram_2_data, \адрес_текущей_инструкции_q ,
       \алу_конечный_1_выход , \регистр_Ё_2_q , \регистр_Ё_q ;

  Adder adder_1 (.a(\адрес_текущей_инструкции_q ), .b(8'h1), .out(adder_1_out));  // open: cin, cout
  assign controlled_buffer_1_out = \выбор_источника_след_инструкции  ? adder_1_out : 8'bz;  // Controlled_Buffer controlled_buffer_1
  assign controlled_buffer_1_out = not_1_out ? \адрес_для_перехода  : 8'bz;  // Controlled_Buffer controlled_buffer_2
  Clock clock_1 (.out(clock_1_out));
  Register \u_адрес_текущей_инструкции  (
    .D(controlled_buffer_1_out), .Q(\адрес_текущей_инструкции_q ), .clk(clock_2_out));  // open: en, clr
  Clock clock_2 (.out(clock_2_out));
  not not_1 (not_1_out, \выбор_источника_след_инструкции );
  Register \u_регистр_Ё  (.D(controlled_buffer_3_out), .Q(\регистр_Ё_q ), .clk(clock_1_out));  // open: en, clr
  assign controlled_buffer_3_out = in_7 ? controlled_buffer_4_out : 8'bz;  // Controlled_Buffer controlled_buffer_3
  assign controlled_buffer_4_out = not_2_out ? \регистр_Ё_q  : 8'bz;  // Controlled_Buffer controlled_buffer_4
  not not_2 (not_2_out, in_7);
  RAM #(.dataWidth(12)) ram_1 (
    .addr(\адрес_текущей_инструкции_q ),
    .data({\дополнительные_данные , \инструкция_с_описаним_действий [3:0]}));  // open: sel, clk, ld, clr
  Register \u_регистр_Ё_2  (.D(controlled_buffer_6_out), .Q(\регистр_Ё_2_q ), .clk(clock_1_out));  // open: en, clr
  assign controlled_buffer_5_out = not_3_out ? \регистр_Ё_2_q  : 8'bz;  // Controlled_Buffer controlled_buffer_5
  not not_3 (not_3_out, in_7);
  RAM #(.addrWidth(4)) ram_2 (
    .addr(\адресный ), .data(ram_2_data), .sel(\память ), .clk(clock_1_out), .ld(in_7));  // open: clr
  assign controlled_buffer_6_out = in_7 ? controlled_buffer_5_out : 8'bz;  // Controlled_Buffer controlled_buffer_6
  Demultiplexer #(.width(8)) demultiplexer_1 (
    .out0(controlled_buffer_4_out), .out1(controlled_buffer_5_out), .in(ram_2_data), .sel(\выбор_регистров ));  // open: en
  \АЛУ_КОНЕЧНЫЙ  \u_алу_конечный_1  (
    ._0(controlled_buffer_5_out), ._1(\регистр_Ё_q ), .\выбор (\выбор_операции ),
    .\выход (\алу_конечный_1_выход ));
  assign controlled_buffer_6_out = not_4_out ? \алу_конечный_1_выход  : 8'bz;  // Controlled_Buffer controlled_buffer_7
  not not_4 (not_4_out, \память );

  assign \инструкция_с_описаним_действий [11:4] = \дополнительные_данные ;
  assign \код_действия  = \инструкция_с_описаним_действий [3:0];

  // Notes on the sheet:
  //   000 - или
  //   001 - и
  //   110 - сравнение
  //   111 - сложение 
  //   010 - число 1, сдвиг влево
  //   011 - число 1, сдвиг вправо
  //   100 - число 2, сдвиг влево
  //   101 - число 2, сдвиг вправо
  //   память с командами
  //   память данных
  //   чтение/запись
  //   0 - чтение
  //   1 - запись 
  //   выбор
  //   выход
endmodule
