// Logisim project схема памяти.circ as structural Verilog: 1 circuit, main circuit main
module main (
  input  \Сброс ,
  input  [3:0] in_2,
  input  [2:0] \Адрес ,
  output [3:0] out_4
);

  wire and_1_out, and_2_out, and_3_out, and_4_out, and_5_out, and_6_out, and_7_out, and_8_out, and_9_out,
       and_10_out, and_11_out, and_12_out, and_13_out, and_14_out, and_15_out, and_16_out, and_17_out,
       and_18_out, and_19_out, and_20_out, and_21_out, and_22_out, and_23_out, and_24_out, and_25_out,
       and_26_out, and_27_out, and_28_out, and_29_out, and_30_out, and_31_out, and_32_out, and_33_out,
       and_34_out, and_35_out, and_36_out, and_37_out, and_38_out, and_39_out, and_40_out, clock_1_out,
       d_ff_1_q, d_ff_2_q, d_ff_3_q, d_ff_4_q, d_ff_5_q, d_ff_6_q, d_ff_7_q, d_ff_8_q, d_ff_9_q, d_ff_10_q,
       d_ff_11_q, d_ff_12_q, d_ff_13_q, d_ff_14_q, d_ff_15_q, d_ff_16_q, d_ff_17_q, d_ff_18_q, d_ff_19_q,
       d_ff_20_q, d_ff_21_q, d_ff_22_q, d_ff_23_q, d_ff_24_q, d_ff_25_q, d_ff_26_q, d_ff_27_q, d_ff_28_q,
       d_ff_29_q, d_ff_30_q, d_ff_31_q, d_ff_32_q, decoder_1_out0, decoder_1_out1, decoder_1_out2,
       decoder_1_out3, decoder_1_out4, decoder_1_out5, decoder_1_out6, decoder_1_out7;

  Decoder #(.select(3)) decoder_1 (
    .out0(decoder_1_out0), .out1(decoder_1_out1), .out2(decoder_1_out2), .out3(decoder_1_out3),
    .out4(decoder_1_out4), .out5(decoder_1_out5), .out6(decoder_1_out6), .out7(decoder_1_out7), .sel(\Адрес ));  // open: en
  Clock clock_1 (.out(clock_1_out));
  and and_1 (and_1_out, clock_1_out, decoder_1_out0);
  and and_2 (and_2_out, clock_1_out, decoder_1_out1);
  and and_3 (and_3_out, clock_1_out, decoder_1_out2);
  and and_4 (and_4_out, clock_1_out, decoder_1_out3);
  and and_5 (and_5_out, clock_1_out, decoder_1_out4);
  and and_6 (and_6_out, clock_1_out, decoder_1_out5);
  and and_7 (and_7_out, clock_1_out, decoder_1_out6);
  and and_8 (and_8_out, clock_1_out, decoder_1_out7);
  D_Flip_Flop d_ff_1 (.clk(and_1_out), .D(in_2[3]), .Q(d_ff_1_q), .reset(\Сброс ));  // open: Qn, preset, en
  and and_9 (and_9_out, decoder_1_out0, d_ff_1_q);
  D_Flip_Flop d_ff_2 (.clk(and_2_out), .D(in_2[3]), .Q(d_ff_2_q), .reset(clock_1_out));  // open: Qn, preset, en
  D_Flip_Flop d_ff_3 (.clk(and_3_out), .D(in_2[3]), .Q(d_ff_3_q), .reset(clock_1_out));  // open: Qn, preset, en
  D_Flip_Flop d_ff_4 (.clk(and_4_out), .D(in_2[3]), .Q(d_ff_4_q), .reset(clock_1_out));  // open: Qn, preset, en
  D_Flip_Flop d_ff_5 (.clk(and_5_out), .D(in_2[3]), .Q(d_ff_5_q), .reset(clock_1_out));  // open: Qn, preset, en
  D_Flip_Flop d_ff_6 (.clk(and_6_out), .D(in_2[3]), .Q(d_ff_6_q), .reset(clock_1_out));  // open: Qn, preset, en
  D_Flip_Flop d_ff_7 (.clk(and_7_out), .D(in_2[3]), .Q(d_ff_7_q), .reset(clock_1_out));  // open: Qn, preset, en
  D_Flip_Flop d_ff_8 (.clk(and_8_out), .D(in_2[3]), .Q(d_ff_8_q), .reset(\Сброс ));  // open: Qn, preset, en
  and and_10 (and_10_out, decoder_1_out1, d_ff_2_q);
  and and_11 (and_11_out, decoder_1_out2, d_ff_3_q);
  and and_12 (and_12_out, decoder_1_out3, d_ff_4_q);
  and and_13 (and_13_out, decoder_1_out4, d_ff_5_q);
  and and_14 (and_14_out, decoder_1_out5, d_ff_6_q);
  and and_15 (and_15_out, decoder_1_out6, d_ff_7_q);
  and and_16 (and_16_out, decoder_1_out7, d_ff_8_q);
  or or_1 (out_4[3], and_16_out, and_15_out, and_14_out, and_13_out, and_12_out, and_11_out, and_10_out, and_9_out);
  D_Flip_Flop d_ff_9 (.clk(and_1_out), .D(in_2[2]), .Q(d_ff_9_q), .reset(\Сброс ));  // open: Qn, preset, en
  and and_17 (and_17_out, decoder_1_out0, d_ff_9_q);
  D_Flip_Flop d_ff_10 (.clk(and_2_out), .D(in_2[2]), .Q(d_ff_10_q), .reset(clock_1_out));  // open: Qn, preset, en
  and and_18 (and_18_out, decoder_1_out1, d_ff_10_q);
  D_Flip_Flop d_ff_11 (.clk(and_3_out), .D(in_2[2]), .Q(d_ff_11_q), .reset(clock_1_out));  // open: Qn, preset, en
  D_Flip_Flop d_ff_12 (.clk(and_4_out), .D(in_2[2]), .Q(d_ff_12_q), .reset(clock_1_out));  // open: Qn, preset, en
  and and_19 (and_19_out, decoder_1_out3, d_ff_12_q);
  D_Flip_Flop d_ff_13 (.clk(and_5_out), .D(and_5_out), .Q(d_ff_13_q), .reset(clock_1_out));  // open: Qn, preset, en
  and and_20 (and_20_out, decoder_1_out4, d_ff_13_q);
  D_Flip_Flop d_ff_14 (.clk(and_6_out), .D(in_2[2]), .Q(d_ff_14_q), .reset(clock_1_out));  // open: Qn, preset, en
  D_Flip_Flop d_ff_15 (.clk(and_7_out), .D(and_7_out), .Q(d_ff_15_q), .reset(clock_1_out));  // open: Qn, preset, en
  and and_21 (and_21_out, decoder_1_out6, d_ff_15_q);
  D_Flip_Flop d_ff_16 (.clk(and_8_out), .D(in_2[2]), .Q(d_ff_16_q), .reset(\Сброс ));  // open: Qn, preset, en
  and and_22 (and_22_out, decoder_1_out7, d_ff_16_q);
  and and_23 (and_23_out, decoder_1_out2, d_ff_11_q);
  and and_24 (and_24_out, decoder_1_out5, d_ff_14_q);
  or or_2 (out_4[2], and_22_out, and_21_out, and_24_out, and_20_out, and_19_out, and_23_out, and_18_out, and_17_out);
  D_Flip_Flop d_ff_17 (.clk(and_1_out), .D(in_2[1]), .Q(d_ff_17_q), .reset(\Сброс ));  // open: Qn, preset, en
  and and_25 (and_25_out, decoder_1_out0, d_ff_17_q);
  D_Flip_Flop d_ff_18 (.clk(and_2_out), .D(in_2[1]), .Q(d_ff_18_q), .reset(clock_1_out));  // open: Qn, preset, en
  and and_26 (and_26_out, decoder_1_out1, d_ff_18_q);
  D_Flip_Flop d_ff_19 (.clk(and_3_out), .D(in_2[1]), .Q(d_ff_19_q), .reset(clock_1_out));  // open: Qn, preset, en
  and and_27 (and_27_out, decoder_1_out2, d_ff_19_q);
  D_Flip_Flop d_ff_20 (.clk(and_4_out), .D(in_2[1]), .Q(d_ff_20_q), .reset(clock_1_out));  // open: Qn, preset, en
  and and_28 (and_28_out, decoder_1_out3, d_ff_20_q);
  D_Flip_Flop d_ff_21 (.clk(and_5_out), .D(in_2[1]), .Q(d_ff_21_q), .reset(clock_1_out));  // open: Qn, preset, en
  and and_29 (and_29_out, decoder_1_out4, d_ff_21_q);
  D_Flip_Flop d_ff_22 (.clk(and_6_out), .D(in_2[1]), .Q(d_ff_22_q), .reset(clock_1_out));  // open: Qn, preset, en
  and and_30 (and_30_out, decoder_1_out5, d_ff_22_q);
  D_Flip_Flop d_ff_23 (.clk(and_7_out), .D(in_2[1]), .Q(d_ff_23_q), .reset(clock_1_out));  // open: Qn, preset, en
  and and_31 (and_31_out, decoder_1_out6, d_ff_23_q);
  D_Flip_Flop d_ff_24 (.clk(and_8_out), .D(in_2[1]), .Q(d_ff_24_q), .reset(\Сброс ));  // open: Qn, preset, en
  and and_32 (and_32_out, decoder_1_out7, d_ff_24_q);
  or or_3 (out_4[1], and_32_out, and_31_out, and_30_out, and_29_out, and_28_out, and_27_out, and_26_out, and_25_out);
  D_Flip_Flop d_ff_25 (.clk(and_1_out), .D(in_2[0]), .Q(d_ff_25_q), .reset(\Сброс ));  // open: Qn, preset, en
  and and_33 (and_33_out, decoder_1_out0, d_ff_25_q);
  D_Flip_Flop d_ff_26 (.clk(and_2_out), .D(in_2[0]), .Q(d_ff_26_q), .reset(clock_1_out));  // open: Qn, preset, en
  and and_34 (and_34_out, decoder_1_out1, d_ff_26_q);
  D_Flip_Flop d_ff_27 (.clk(and_3_out), .D(in_2[0]), .Q(d_ff_27_q), .reset(clock_1_out));  // open: Qn, preset, en
  D_Flip_Flop d_ff_28 (.clk(and_4_out), .D(in_2[0]), .Q(d_ff_28_q), .reset(clock_1_out));  // open: Qn, preset, en
  and and_35 (and_35_out, decoder_1_out3, d_ff_28_q);
  D_Flip_Flop d_ff_29 (.clk(and_5_out), .D(in_2[0]), .Q(d_ff_29_q), .reset(clock_1_out));  // open: Qn, preset, en
  and and_36 (and_36_out, decoder_1_out4, d_ff_29_q);
  D_Flip_Flop d_ff_30 (.clk(and_6_out), .D(in_2[0]), .Q(d_ff_30_q), .reset(clock_1_out));  // open: Qn, preset, en
  D_Flip_Flop d_ff_31 (.clk(and_7_out), .D(in_2[0]), .Q(d_ff_31_q), .reset(clock_1_out));  // open: Qn, preset, en
  and and_37 (and_37_out, decoder_1_out6, d_ff_31_q);
  D_Flip_Flop d_ff_32 (.clk(and_8_out), .D(in_2[0]), .Q(d_ff_32_q), .reset(\Сброс ));  // open: Qn, preset, en
  and and_38 (and_38_out, decoder_1_out7, d_ff_32_q);
  and and_39 (and_39_out, decoder_1_out2, d_ff_27_q);
  and and_40 (and_40_out, decoder_1_out5, d_ff_30_q);
  or or_4 (out_4[0], and_38_out, and_37_out, and_40_out, and_36_out, and_35_out, and_39_out, and_34_out, and_33_out);

  // Notes on the sheet:
  //   Кобяшова Д.А
  //   Схема памяти
  //   Данные для записи
  //   Чтение данных
endmodule
